# Fritzing sketch BUGGY(1) (saved by Fritzing 1.0.2b)
breadboards: 1

parts:
  M1 = gear-motor-encoder-magnet
  M3 = MH Sensor Series 4-pin IR Sensor/Line follower [package=THT]
  M4 = MH Sensor Series 4-pin IR Sensor/Line follower [package=THT]
  BAT1 = 6xAA battery
  Part2 = SRF05 Ultrasonic Rangefinder
  M2 = gear-motor-encoder-magnet
  IC2 = H-Bridge [package=THT]  # not connected
  Part1 = Adafruit Proto Shield R3 [part_number="Adafruit #2077"]

nets:
  N1: M1.pin_1, Part1.D7#D7, Part1.E7
  N2: M1.pin_2, Part1.D10#D10, Part1.E10
  N3: M3.pin2, Part1.D2
  GND: M3.pin3, M4.pin3, BAT1.Pin_1, Part2.GND, Part1.D8#D8, Part1.D9, Part1.E8, Part1.E9, Part1.F8, Part1.F9, Part1.F17, Part1.G8, Part1.G9, Part1.G17, Part1.H17, Part1.I17, Part1.J17, Part1.GND
  VCC: M3.pin4, M4.pin4, Part2.VCC, Part1.F12, Part1.G12, Part1.+5V
  N4: M4.pin2, Part1.D13
  N5: BAT1.Pin_2, Part1.D5#D5, Part1.E5, Part1.VIN
  N6: Part2.Trig, Part1.D7#88
  N7: Part2.Echo, Part1.D8#89
  N8: M2.pin_1, Part1.F10, Part1.G10
  N9: M2.pin_2, Part1.F7, Part1.G7
  N10: Part1.D6#D6, Part1.E6, Part1.D12#93
  N11: Part1.D11#D11, Part1.E11, Part1.D5#86
  N12: Part1.D12#D12, Part1.E12, Part1.D3
  N13: Part1.F5, Part1.G5, Part1.D10#91
  N14: Part1.F6, Part1.G6, Part1.D6#87
  N15: Part1.F11, Part1.G11, Part1.D11#92

custom parts:
  gear-motor-encoder-magnet: Generic gear motor, 3V to 6V, dual output shafts, 1:48 gear ratio with magnet for wheel encoder
  MH Sensor Series 4-pin IR Sensor/Line follower: modified version of FC-51 from Peter Van Epp (vanepp in forums) This is the 4-pin version of IR line follower module, using the TCRT5000 sensor and LM393 comparator This one has the analogue output pin, in addition to the Digital pin which is set by the trimmer. The Analog pin can feed an Arduino ADC input, for much better level sensing options and less drift than the crappy potentiometer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
  Adafruit Proto Shield R3: This prototyping shield is the best out there (well, we think so, at least), and now is even better with Version R3 - updated for the most compatibility with just about all the Arduinos! It works with UNO, Mega, Leonardo, NG, Diecimila, Duemilanove, and compatible Arduinos. Yun's and Arduino Ethernets have a chunky Ethernet jack that gets in the way of stacking, you can use the stacking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
